# Fritzing sketch IDD (saved by Fritzing 0.9.4)
breadboards: 1

parts:
  WeMos_D1_Mini1 = WeMos D1 Mini
  S1 = Square Pushbutton
  R1 = Resistor [tolerance=±5% resistance=330 package="0603 [SMD]"]
  R2 = Resistor [tolerance=±5% resistance=1k package="0603 [SMD]"]
  LED1 = smd LED [color="Red (633nm)" package="1206 [SMD]"]
  WeMos_D1_Mini2 = WeMos D1 Mini
  S2 = Square Pushbutton
  R3 = Resistor [tolerance=±5% resistance=330 package="0603 [SMD]"]
  LED2 = smd LED [color="Red (633nm)" package="1206 [SMD]"]
  R5 = Resistor [tolerance=±5% resistance=1k package="0603 [SMD]"]

nets:
  N1: WeMos_D1_Mini1.D5, S1.leg0, R1.Pin_0
  N2: R1.Pin_1, R2.Pin_0
  N3: R2.Pin_1, LED1.cathode
  N4: WeMos_D1_Mini2.3V3, S2.leg0
  N5: WeMos_D1_Mini2.D5, S2.leg1, R3.Pin_1
  N6: WeMos_D1_Mini2.D8, LED2.anode
  N7: R3.Pin_0, R5.Pin_0

notes:
  4v-6v VIN
